# Fritzing sketch Circuit (saved by Fritzing 0.9.3b)
circuit board: 11.3015cm x 7.40891cm
breadboards: 1

parts:
  Part1 = Arduino Nano (Rev3.0)
  Even = Header 12 [package=1x12_machine-pin-header_lock.004]
  Odd = Header 12 [package=1x12_machine-pin-header_lock.004]
  Pot_1 = Header 3 [package=molex-1x3_lock]
  pot2 = Header 3 [package=molex-1x3_lock]
  pot3 = Header 3 [package=molex-1x3_lock]
  Buzzer = Header 3 [package=molex-1x3_lock]
  L298N = Header 6 [package=molex-1x6_lock]
  X1 = USB Connectors [package=usb-a-h]

nets:
  GND: Part1.GND, Pot_1.1, pot2.1, pot3.1, Buzzer.1, X1.GND
  N1: Part1.D2, Buzzer.2
  N2: Part1.D3, L298N.1
  N3: Part1.D4, L298N.2
  N4: Part1.D5, L298N.3
  N5: Part1.D6, L298N.4
  N6: Part1.D7, L298N.5
  N7: Part1.D8, L298N.6
  VIN: Part1.VIN, Part1.5V, Pot_1.3, pot2.3, pot3.3, Buzzer.3, X1.VBUS
  N8: Part1.A2, Odd.3
  N9: Part1.A1, Odd.2
  N10: Part1.A0, Odd.1
  N11: Even.1, Pot_1.2
  N12: Even.2, pot2.2
  N13: Even.3, pot3.2
